// Logisim project version1.circ as structural Verilog: 6 circuits, main circuit main
module main (
  output [7:0] out_1,
  output [2:0] out_2
);

  wire and_1_out, clock_1_out, control_unit_1_alo, control_unit_1_als, control_unit_1_ao, control_unit_1_aw,
       control_unit_1_bo, control_unit_1_bw, control_unit_1_fw, control_unit_1_hlt, control_unit_1_irw,
       control_unit_1_ml, control_unit_1_mo, control_unit_1_mw, control_unit_1_ow, control_unit_1_pci,
       control_unit_1_pco, control_unit_1_pcw, not_1_out, RST_out;
  wire [1:0] alu_1_fc, register_1_q;
  wire [3:0] register_8_bit_3_rout, register_8_bit_3_rout_2, register_8_bit_4_rout, register_8_bit_4_rout_2,
       register_8_bit_5_rout, register_8_bit_5_rout_2;
  wire [7:0] ram_1_dout, register_8_bit_1_rout, register_8_bit_2_rout;

  Clock clock_1 (.out(clock_1_out));
  and and_1 (and_1_out, clock_1_out, not_1_out);
  not not_1 (not_1_out, control_unit_1_hlt);
  Button RST (.out(RST_out));
  RAM #(.enables("line")) ram_1 (
    .addr(register_8_bit_1_rout), .we(control_unit_1_mw), .clk(and_1_out), .din(out_1), .dout(ram_1_dout));
  counter_8_bit counter_8_bit_1 (
    .WE(control_unit_1_pcw), .OE(control_unit_1_pco), .INC(control_unit_1_pci), .RST(RST_out),
    .CLK(and_1_out), .PCI(out_1), .PCO(out_1));  // open: PCOO
  register_8_bit register_8_bit_1 (
    .RST(RST_out), .CLK(and_1_out), .WE(control_unit_1_ml), .RIN(out_1), .ROUT(register_8_bit_1_rout));  // open: OE, ROUT_tri
  register_8_bit register_8_bit_2 (
    .RST(RST_out), .CLK(and_1_out), .WE(control_unit_1_irw), .RIN(out_1), .ROUT(register_8_bit_2_rout));  // open: OE, ROUT_tri
  assign out_1 = control_unit_1_mo ? ram_1_dout : 8'bz;  // Controlled_Buffer controlled_buffer_1
  control_unit control_unit_1 (
    .RST(RST_out), .CLK(and_1_out), .INSTR(register_8_bit_2_rout), .FLG(register_1_q), .mcrstp(out_2),
    .HLT(control_unit_1_hlt), .ALO(control_unit_1_alo), .ALS(control_unit_1_als), .FW(control_unit_1_fw),
    .OW(control_unit_1_ow), .BO(control_unit_1_bo), .BW(control_unit_1_bw), .AO(control_unit_1_ao),
    .AW(control_unit_1_aw), .IRW(control_unit_1_irw), .MW(control_unit_1_mw), .MO(control_unit_1_mo),
    .ML(control_unit_1_ml), .PCI(control_unit_1_pci), .PCO(control_unit_1_pco), .PCW(control_unit_1_pcw));
  register_8_bit register_8_bit_3 (
    .OE(control_unit_1_ao), .RST(RST_out), .CLK(and_1_out), .WE(control_unit_1_aw), .RIN(out_1),
    .ROUT({register_8_bit_3_rout_2, register_8_bit_3_rout}), .ROUT_tri(out_1));
  alu alu_1 (
    .OE(control_unit_1_alo), .SUB(control_unit_1_als),
    .ALI1({register_8_bit_3_rout_2, register_8_bit_3_rout}),
    .ALI2({register_8_bit_4_rout_2, register_8_bit_4_rout}), .FC(alu_1_fc[0]), .FZ(alu_1_fc[1]), .ALO(out_1));
  register_8_bit register_8_bit_4 (
    .OE(control_unit_1_bo), .RST(RST_out), .CLK(and_1_out), .WE(control_unit_1_bw), .RIN(out_1),
    .ROUT({register_8_bit_4_rout_2, register_8_bit_4_rout}), .ROUT_tri(out_1));
  register_8_bit register_8_bit_5 (
    .RST(RST_out), .CLK(and_1_out), .WE(control_unit_1_ow), .RIN(out_1),
    .ROUT({register_8_bit_5_rout_2, register_8_bit_5_rout}));  // open: OE, ROUT_tri
  Register #(.width(2)) register_1 (
    .D(alu_1_fc), .en(control_unit_1_fw), .clk(and_1_out), .Q(register_1_q), .clr(RST_out));
  Hex_Digit_Display hex_digit_display_1 (.value(register_8_bit_3_rout_2));  // open: dp
  Hex_Digit_Display hex_digit_display_2 (.value(register_8_bit_3_rout));  // open: dp
  Hex_Digit_Display hex_digit_display_3 (.value(register_8_bit_4_rout_2));  // open: dp
  Hex_Digit_Display hex_digit_display_4 (.value(register_8_bit_4_rout));  // open: dp
  Hex_Digit_Display hex_digit_display_5 (.value(register_8_bit_5_rout_2));  // open: dp
  Hex_Digit_Display hex_digit_display_6 (.value(register_8_bit_5_rout));  // open: dp

  // Notes on the sheet:
  //   PC
  //   MAR
  //   IR
  //   A
  //   ALU
  //   B
  //   OUT
  //   A Register
  //   B Register
  //   OUT
endmodule

module counter_8_bit (
  input  OE,
  input  INC,
  input  RST,
  input  CLK,
  input  [7:0] PCI,
  input  WE,
  output [7:0] PCO,
  output [7:0] PCOO
);

  wire and_1_out, and_2_out, and_3_out, and_4_out, and_5_out, and_6_out, and_7_out, and_8_out, and_9_out,
       and_10_out, and_11_out, and_12_out, and_13_out, and_14_out, and_15_out, and_16_out, j_k_ff_1_qn,
       j_k_ff_2_qn, j_k_ff_3_qn, j_k_ff_4_qn, j_k_ff_5_qn, j_k_ff_6_qn, j_k_ff_7_qn, not_1_out, not_2_out,
       not_3_out, not_4_out, not_5_out, not_6_out, not_7_out, not_8_out, or_1_out, or_2_out, or_3_out,
       or_4_out, or_5_out, or_6_out, or_7_out, or_8_out;

  not not_1 (not_1_out, PCI[0]);
  and and_1 (and_1_out, PCI[0], WE);
  and and_2 (and_2_out, not_1_out, WE);
  J_K_Flip_Flop j_k_ff_1 (
    .J(INC), .K(INC), .clk(CLK), .Q(PCOO[0]), .Qn(j_k_ff_1_qn), .preset(and_1_out), .reset(or_1_out));
  or or_1 (or_1_out, RST, and_2_out);
  not not_2 (not_2_out, PCI[1]);
  and and_3 (and_3_out, PCI[1], WE);
  and and_4 (and_4_out, not_2_out, WE);
  J_K_Flip_Flop j_k_ff_2 (
    .J(INC), .K(INC), .clk(j_k_ff_1_qn), .Q(PCOO[1]), .Qn(j_k_ff_2_qn), .preset(and_3_out), .reset(or_2_out));
  or or_2 (or_2_out, RST, and_4_out);
  not not_3 (not_3_out, PCI[2]);
  and and_5 (and_5_out, PCI[2], WE);
  J_K_Flip_Flop j_k_ff_3 (
    .J(INC), .K(INC), .clk(j_k_ff_2_qn), .Q(PCOO[2]), .Qn(j_k_ff_3_qn), .preset(and_5_out), .reset(or_3_out));
  or or_3 (or_3_out, RST, and_6_out);
  and and_6 (and_6_out, not_3_out, WE);
  and and_7 (and_7_out, PCI[3], WE);
  J_K_Flip_Flop j_k_ff_4 (
    .J(INC), .K(INC), .clk(j_k_ff_3_qn), .Q(PCOO[3]), .Qn(j_k_ff_4_qn), .preset(and_7_out), .reset(or_4_out));
  or or_4 (or_4_out, RST, and_8_out);
  not not_4 (not_4_out, PCI[3]);
  and and_8 (and_8_out, not_4_out, WE);
  and and_9 (and_9_out, PCI[4], WE);
  J_K_Flip_Flop j_k_ff_5 (
    .J(INC), .K(INC), .clk(j_k_ff_4_qn), .Q(PCOO[4]), .Qn(j_k_ff_5_qn), .preset(and_9_out), .reset(or_5_out));
  or or_5 (or_5_out, RST, and_10_out);
  assign PCO = OE ? PCOO : 8'bz;  // Controlled_Buffer controlled_buffer_1
  not not_5 (not_5_out, PCI[4]);
  and and_10 (and_10_out, not_5_out, WE);
  and and_11 (and_11_out, PCI[5], WE);
  J_K_Flip_Flop j_k_ff_6 (
    .J(INC), .K(INC), .clk(j_k_ff_5_qn), .Q(PCOO[5]), .Qn(j_k_ff_6_qn), .preset(and_11_out), .reset(or_6_out));
  or or_6 (or_6_out, RST, and_12_out);
  not not_6 (not_6_out, PCI[5]);
  and and_12 (and_12_out, not_6_out, WE);
  J_K_Flip_Flop j_k_ff_7 (
    .J(INC), .K(INC), .clk(j_k_ff_6_qn), .Q(PCOO[6]), .Qn(j_k_ff_7_qn), .preset(and_13_out), .reset(or_7_out));
  not not_7 (not_7_out, PCI[6]);
  and and_13 (and_13_out, PCI[6], WE);
  and and_14 (and_14_out, not_7_out, WE);
  J_K_Flip_Flop j_k_ff_8 (
    .J(INC), .K(INC), .clk(j_k_ff_7_qn), .Q(PCOO[7]), .preset(and_16_out), .reset(or_8_out));  // open: Qn
  or or_7 (or_7_out, RST, and_14_out);
  not not_8 (not_8_out, PCI[7]);
  and and_15 (and_15_out, not_8_out, WE);
  and and_16 (and_16_out, PCI[7], WE);
  or or_8 (or_8_out, RST, and_15_out);
endmodule

module register_8_bit (
  input  OE,
  input  RST,
  input  CLK,
  input  WE,
  input  [7:0] RIN,
  output [7:0] ROUT,
  output [7:0] ROUT_tri
);

  Register #(.width(1)) register_1 (.D(RIN[7]), .en(WE), .clk(CLK), .Q(ROUT[7]), .clr(RST));
  Register #(.width(1)) register_2 (.D(RIN[6]), .en(WE), .clk(CLK), .Q(ROUT[6]), .clr(RST));
  Register #(.width(1)) register_3 (.D(RIN[5]), .en(WE), .clk(CLK), .Q(ROUT[5]), .clr(RST));
  Register #(.width(1)) register_4 (.D(RIN[4]), .en(WE), .clk(CLK), .Q(ROUT[4]), .clr(RST));
  Register #(.width(1)) register_5 (.D(RIN[3]), .en(WE), .clk(CLK), .Q(ROUT[3]), .clr(RST));
  Register #(.width(1)) register_6 (.D(RIN[2]), .en(WE), .clk(CLK), .Q(ROUT[2]), .clr(RST));
  assign ROUT_tri = OE ? ROUT : 8'bz;  // Controlled_Buffer controlled_buffer_1
  Register #(.width(1)) register_7 (.D(RIN[1]), .en(WE), .clk(CLK), .Q(ROUT[1]), .clr(RST));
  Register #(.width(1)) register_8 (.D(RIN[0]), .en(WE), .clk(CLK), .Q(ROUT[0]), .clr(RST));
endmodule

module alu (
  input  OE,
  input  SUB,
  input  [7:0] ALI1,
  input  [7:0] ALI2,
  output FZ,
  output [7:0] ALO,
  output FC
);

  wire adder_1_cout, adder_2_cout, adder_3_cout, adder_4_cout, adder_5_cout, adder_6_cout, adder_7_cout,
       xor_1_out, xor_2_out, xor_3_out, xor_4_out, xor_5_out, xor_6_out, xor_7_out, xor_8_out;
  wire [7:0] adder_1_out;

  nor nor_1 (FZ, adder_1_out[0], adder_1_out[1], adder_1_out[2], adder_1_out[3], adder_1_out[4], adder_1_out[5], adder_1_out[6], adder_1_out[7]);
  xor xor_1 (xor_1_out, ALI2[0], SUB);
  Adder #(.width(1)) adder_1 (.a(xor_1_out), .b(ALI1[0]), .out(adder_1_out[0]), .cin(SUB), .cout(adder_1_cout));
  xor xor_2 (xor_2_out, ALI2[1], SUB);
  Adder #(.width(1)) adder_2 (
    .a(xor_2_out), .b(ALI1[1]), .out(adder_1_out[1]), .cin(adder_1_cout), .cout(adder_2_cout));
  xor xor_3 (xor_3_out, ALI2[2], SUB);
  Adder #(.width(1)) adder_3 (
    .a(xor_3_out), .b(ALI1[2]), .out(adder_1_out[2]), .cin(adder_2_cout), .cout(adder_3_cout));
  xor xor_4 (xor_4_out, ALI2[3], SUB);
  xor xor_5 (xor_5_out, ALI2[4], SUB);
  Adder #(.width(1)) adder_4 (
    .a(xor_4_out), .b(ALI1[3]), .out(adder_1_out[3]), .cin(adder_3_cout), .cout(adder_4_cout));
  assign ALO = OE ? adder_1_out : 8'bz;  // Controlled_Buffer controlled_buffer_1
  xor xor_6 (xor_6_out, ALI2[5], SUB);
  Adder #(.width(1)) adder_5 (
    .a(xor_5_out), .b(ALI1[4]), .out(adder_1_out[4]), .cin(adder_4_cout), .cout(adder_5_cout));
  xor xor_7 (xor_7_out, ALI2[6], SUB);
  Adder #(.width(1)) adder_6 (
    .a(xor_6_out), .b(ALI1[5]), .out(adder_1_out[5]), .cin(adder_5_cout), .cout(adder_6_cout));
  Adder #(.width(1)) adder_7 (
    .a(xor_7_out), .b(ALI1[6]), .out(adder_1_out[6]), .cin(adder_6_cout), .cout(adder_7_cout));
  xor xor_8 (xor_8_out, ALI2[7], SUB);
  Adder #(.width(1)) adder_8 (.a(xor_8_out), .b(ALI1[7]), .out(adder_1_out[7]), .cin(adder_7_cout), .cout(FC));
endmodule

module control_unit (
  input  RST,
  input  CLK,
  input  [7:0] INSTR,
  input  [1:0] FLG,
  output [2:0] mcrstp,
  output HLT,
  output ALO,
  output ALS,
  output FW,
  output OW,
  output BO,
  output BW,
  output AO,
  output AW,
  output IRW,
  output MW,
  output MO,
  output ML,
  output PCI,
  output PCO,
  output PCW
);

  wire or_1_out;
  wire [3:3] rom_1_data;

  or or_1 (or_1_out, RST, rom_1_data[3]);
  counter_3_bit_falling_edge counter_3_bit_falling_edge_1 (.INC(1'b1), .RST(or_1_out), .CLK(CLK), .CO(mcrstp));
  ROM #(.addrWidth(10), .dataWidth(17)) rom_1 (
    .addr({INSTR[4:0], FLG, mcrstp}),
    .data({HLT, ALO, ALS, FW, OW, BO, BW, AO, AW, IRW, MW, MO, ML, rom_1_data[3], PCI, PCO, PCW}));

  // Notes on the sheet:
  //   contents of rom_1 (hex, n*v repeats v):
  //   12 a4 8 5*10000 12 a4 8 5*10000 12 a4 8 5*10000 12 a4 8 5*10000 12 a4 6*10000 12 a4 6*10000 12 a4
  //   6*10000 12 a4 6*10000 12 a4 12 124 8 10000 10000 10000 12 a4 12 124 8 10000 10000 10000 12 a4 12 124
  //   8 10000 10000 10000 12 a4 12 124 8 10000 10000 10000 12 a4 12 34 124 8 10000 10000 12 a4 12 34 124 8
  //   10000 10000 12 a4 12 34 124 8 10000 10000 12 a4 12 34 124 8 10000 10000 12 a4 12 34 240 8 10000
  //   10000 12 a4 12 34 240 8 10000 10000 12 a4 12 34 240 8 10000 10000 12 a4 12 34 240 8 10000 10000 12
  //   a4 12 424 8 10000 10000 10000 12 a4 12 424 8 10000 10000 10000 12 a4 12 424 8 10000 10000 10000 12
  //   a4 12 424 8 10000 10000 10000 12 a4 12 34 424 8 10000 10000 12 a4 12 34 424 8 10000 10000 12 a4 12
  //   34 424 8 10000 10000 12 a4 12 34 424 8 10000 10000 12 a4 12 34 840 8 10000 10000 12 a4 12 34 840 8
  //   10000 10000 12 a4 12 34 840 8 10000 10000 12 a4 12 34 840 8 10000 10000 12 a4 a100 8 4*10000 12 a4
  //   a100 8 4*10000 12 a4 a100 8 4*10000 12 a4 a100 8 4*10000 12 a4 e100 8 4*10000 12 a4 e100 8 4*10000
  //   12 a4 e100 8 4*10000 12 a4 e100 8 4*10000 12 a4 1200 8 4*10000 12 a4 1200 8 4*10000 12 a4 1200 8
  //   4*10000 12 a4 1200 8 4*10000 12 a4 12 21 8 10000 10000 10000 12 a4 12 21 8 10000 10000 10000 12 a4
  //   12 21 8 10000 10000 10000 12 a4 12 21 8 10000 10000 10000 12 a4 12 4 8 10000 10000 10000 12 a4 12 21
  //   8 10000 10000 10000 12 a4 12 4 8 10000 10000 10000 12 a4 12 21 8 10000 10000 10000 12 a4 12 4 8
  //   10000 10000 10000 12 a4 12 4 8 10000 10000 10000 12 a4 12 21 8 10000 10000 10000 12 a4 12 21 8 10000
  //   10000 10000 12 a4 6*10000 12 a4 6*10000 12 a4 6*10000 12 a4 6*10000 12 a4 6*10000 12 a4 6*10000 12
  //   a4 6*10000 12 a4 6*10000 12 a4 6*10000 12 a4 6*10000 12 a4 6*10000 12 a4 6*10000 12 a4 6*10000 12 a4
  //   6*10000 12 a4 6*10000 12 a4 6*10000 12 a4 6*10000 12 a4 6*10000 12 a4 6*10000 12 a4 6*10000 12 a4
  //   6*10000 12 a4 6*10000 12 a4 6*10000 12 a4 6*10000 12 a4 6*10000 12 a4 6*10000 12 a4 6*10000 12 a4
  //   6*10000 12 a4 6*10000 12 a4 6*10000 12 a4 6*10000 12 a4 6*10000 12 a4 6*10000 12 a4 6*10000 12 a4
  //   6*10000 12 a4 6*10000 12 a4 6*10000 12 a4 6*10000 12 a4 6*10000 12 a4 6*10000 12 a4 6*10000 12 a4
  //   6*10000 12 a4 6*10000 12 a4 6*10000 12 a4 6*10000 12 a4 6*10000 12 a4 6*10000 12 a4 6*10000 12 a4
  //   6*10000 12 a4 6*10000 12 a4 6*10000 12 a4 6*10000 12 a4 6*10000 12 a4 6*10000 12 a4 6*10000 12 a4
  //   6*10000 12 a4 6*10000 12 a4 6*10000 12 a4 6*10000 12 a4 6*10000 12 a4 6*10000 12 a4 6*10000 12 a4
  //   6*10000 12 a4 6*10000 12 a4 6*10000 12 a4 6*10000 12 a4 6*10000 12 a4 6*10000 12 a4 6*10000 12 a4
  //   6*10000 12 a4 6*10000 12 a4 6*10000
endmodule

module counter_3_bit_falling_edge (
  input  INC,
  input  RST,
  input  CLK,
  output [2:0] CO
);

  J_K_Flip_Flop #(.trigger("falling")) j_k_ff_1 (
    .J(INC), .K(INC), .clk(CLK), .Q(CO[0]), .reset(RST));  // open: Qn, preset
  J_K_Flip_Flop #(.trigger("falling")) j_k_ff_2 (
    .J(INC), .K(INC), .clk(CO[0]), .Q(CO[1]), .reset(RST));  // open: Qn, preset
  J_K_Flip_Flop #(.trigger("falling")) j_k_ff_3 (
    .J(INC), .K(INC), .clk(CO[1]), .Q(CO[2]), .reset(RST));  // open: Qn, preset
endmodule
